// Logisim project hw5evolution.circ as structural Verilog: 11 circuits, main circuit MyXOR
module MyXOR (
  input  x,
  input  y,
  output exhor
);

  wire and_1_out, and_2_out, not_1_out, not_2_out;

  not not_1 (not_1_out, x);
  not not_2 (not_2_out, y);
  and and_1 (and_1_out, not_1_out, y);
  and and_2 (and_2_out, x, not_2_out);
  or or_1 (exhor, and_1_out, and_2_out);

  // Notes on the sheet:
  //   Here is a location to build an XOR circuit
  //   You can follow the tutorial (Help menu - "tutorial") or work on your own...
endmodule

module FullAdder (
  input  X,
  input  Y,
  input  CarryIn,
  output Sum,
  output CarryOut
);

  wire A_out, B_out, C_out, D_out, E_out, F_out, G_out, H_out, not_1_out, not_2_out, not_3_out;

  not not_1 (not_1_out, X);
  not not_2 (not_2_out, Y);
  not not_3 (not_3_out, CarryIn);
  and A (A_out, not_1_out, not_2_out, CarryIn);
  and B (B_out, not_1_out, Y, not_3_out);
  and C (C_out, X, not_2_out, not_3_out);
  and D (D_out, X, Y, CarryIn);
  and E (E_out, not_1_out, Y, CarryIn);
  and F (F_out, X, not_2_out, CarryIn);
  and G (G_out, X, Y, not_3_out);
  and H (H_out, X, Y, CarryIn);
  or or_1 (Sum, A_out, B_out, C_out, D_out);
  or or_2 (CarryOut, E_out, F_out, G_out, H_out);

  // Notes on the sheet:
  //   3 input bits:  X,  Y,  and CarryIn
  //   Here is a location to build an FULL ADDER circuit
  //   (1) draw the other four rails   (2) you'll need 8 AND gates    (3)  you'll need 2 OR gates
  //   two output bits:  Sum and CarryOut
endmodule

module A_4bit_Ripple_Carry_Adder (
  input  Y3,
  input  Y2,
  input  Y1,
  input  Y0,
  input  X3,
  input  X2,
  input  X1,
  input  X0,
  output Sum4,
  output Sum3,
  output Sum2,
  output Sum1,
  output Sum0
);

  wire fulladder_2_carryout, fulladder_3_carryout, fulladder_4_carryout;

  FullAdder fulladder_1 (.X(X3), .Y(Y3), .CarryIn(fulladder_2_carryout), .Sum(Sum3), .CarryOut(Sum4));
  FullAdder fulladder_2 (.X(X2), .Y(Y2), .CarryIn(fulladder_3_carryout), .Sum(Sum2), .CarryOut(fulladder_2_carryout));
  FullAdder fulladder_3 (.X(X1), .Y(Y1), .CarryIn(fulladder_4_carryout), .Sum(Sum1), .CarryOut(fulladder_3_carryout));
  FullAdder fulladder_4 (.X(X0), .Y(Y0), .CarryIn(1'b0), .Sum(Sum0), .CarryOut(fulladder_4_carryout));

  // Notes on the sheet:
  //   Here is a location to build an 4-bit RIPPLE-CARRY ADDER circuit
  //   8 input bits
  //   5 output bits
endmodule

module A_4bit_Multiplier (
  input  Y3,
  input  Y2,
  input  Y1,
  input  Y0,
  input  X3,
  input  X2,
  input  X1,
  input  X0,
  input  in_9,
  output Z7,
  output Z6,
  output Z5,
  output Z4,
  output Z3,
  output Z2,
  output Z1,
  output Z0
);

  wire a_4bit_ripple_carry_adder_1_sum1, a_4bit_ripple_carry_adder_1_sum2, a_4bit_ripple_carry_adder_1_sum3,
       a_4bit_ripple_carry_adder_1_sum4, a_4bit_ripple_carry_adder_3_sum1, a_4bit_ripple_carry_adder_3_sum2,
       a_4bit_ripple_carry_adder_3_sum3, a_4bit_ripple_carry_adder_3_sum4, a_4x1_multiplier_1_out_0,
       a_4x1_multiplier_1_out_1, a_4x1_multiplier_1_out_2, a_4x1_multiplier_1_out_3,
       a_4x1_multiplier_2_out_0, a_4x1_multiplier_2_out_1, a_4x1_multiplier_2_out_2,
       a_4x1_multiplier_2_out_3, a_4x1_multiplier_3_out_0, a_4x1_multiplier_3_out_1,
       a_4x1_multiplier_3_out_2, a_4x1_multiplier_3_out_3, a_4x1_multiplier_4_out_1,
       a_4x1_multiplier_4_out_2, a_4x1_multiplier_4_out_3;

  A_4x1_multiplier a_4x1_multiplier_1 (
    .in_3(Y3), .in_2(Y2), .in_1(Y1), .in_0(Y0), .mult_bit(X3), .out_0(a_4x1_multiplier_1_out_0),
    .out_1(a_4x1_multiplier_1_out_1), .out_2(a_4x1_multiplier_1_out_2), .out_3(a_4x1_multiplier_1_out_3));
  A_4x1_multiplier a_4x1_multiplier_2 (
    .in_3(Y3), .in_2(Y2), .in_1(Y1), .in_0(Y0), .mult_bit(X2), .out_0(a_4x1_multiplier_2_out_0),
    .out_1(a_4x1_multiplier_2_out_1), .out_2(a_4x1_multiplier_2_out_2), .out_3(a_4x1_multiplier_2_out_3));
  A_4x1_multiplier a_4x1_multiplier_3 (
    .in_3(Y3), .in_2(Y2), .in_1(Y1), .in_0(Y0), .mult_bit(X1), .out_0(a_4x1_multiplier_3_out_0),
    .out_1(a_4x1_multiplier_3_out_1), .out_2(a_4x1_multiplier_3_out_2), .out_3(a_4x1_multiplier_3_out_3));
  A_4x1_multiplier a_4x1_multiplier_4 (
    .in_3(Y3), .in_2(Y2), .in_1(Y1), .in_0(Y0), .mult_bit(X0), .out_0(Z0), .out_1(a_4x1_multiplier_4_out_1),
    .out_2(a_4x1_multiplier_4_out_2), .out_3(a_4x1_multiplier_4_out_3));
  A_4bit_Ripple_Carry_Adder a_4bit_ripple_carry_adder_1 (
    .Y3(a_4x1_multiplier_3_out_3), .Y2(a_4x1_multiplier_3_out_2), .Y1(a_4x1_multiplier_3_out_1),
    .Y0(a_4x1_multiplier_3_out_0), .X3(in_9), .X2(a_4x1_multiplier_4_out_3), .X1(a_4x1_multiplier_4_out_2),
    .X0(a_4x1_multiplier_4_out_1), .Sum4(a_4bit_ripple_carry_adder_1_sum4),
    .Sum3(a_4bit_ripple_carry_adder_1_sum3), .Sum2(a_4bit_ripple_carry_adder_1_sum2),
    .Sum1(a_4bit_ripple_carry_adder_1_sum1), .Sum0(Z1));
  A_4bit_Ripple_Carry_Adder a_4bit_ripple_carry_adder_2 (
    .Y3(a_4x1_multiplier_1_out_3), .Y2(a_4x1_multiplier_1_out_2), .Y1(a_4x1_multiplier_1_out_1),
    .Y0(a_4x1_multiplier_1_out_0), .X3(a_4bit_ripple_carry_adder_3_sum4),
    .X2(a_4bit_ripple_carry_adder_3_sum3), .X1(a_4bit_ripple_carry_adder_3_sum2),
    .X0(a_4bit_ripple_carry_adder_3_sum1), .Sum4(Z7), .Sum3(Z6), .Sum2(Z5), .Sum1(Z4), .Sum0(Z3));
  A_4bit_Ripple_Carry_Adder a_4bit_ripple_carry_adder_3 (
    .Y3(a_4x1_multiplier_2_out_3), .Y2(a_4x1_multiplier_2_out_2), .Y1(a_4x1_multiplier_2_out_1),
    .Y0(a_4x1_multiplier_2_out_0), .X3(a_4bit_ripple_carry_adder_1_sum4),
    .X2(a_4bit_ripple_carry_adder_1_sum3), .X1(a_4bit_ripple_carry_adder_1_sum2),
    .X0(a_4bit_ripple_carry_adder_1_sum1), .Sum4(a_4bit_ripple_carry_adder_3_sum4),
    .Sum3(a_4bit_ripple_carry_adder_3_sum3), .Sum2(a_4bit_ripple_carry_adder_3_sum2),
    .Sum1(a_4bit_ripple_carry_adder_3_sum1), .Sum0(Z2));

  // Notes on the sheet:
  //   factor (4 bits)
  //   See the problem for details on this hint:   Build a 4x1-bit multiplier first!
  //   second factor (4 bits)
  //   product (8 bits)
  //   4-bit MULTIPLIER circuit
  //   most significant (highest) output bit
  //   least significant (lowest) output bit
endmodule

module A_3by2_divider (
  input  Y2,
  input  Y1,
  input  Y0,
  input  X1,
  input  X0,
  output Z2,
  output Z1,
  output Z0,
  output Error
);

  wire a_3by2dividor1_1_z0, a_3by2dividor1_1_z1, a_3by2dividor1_1_z2, a_3by2dividor2_1_z0,
       a_3by2dividor2_1_z1, a_3by2dividor2_1_z2, a_3by2dividor3_1_z0, a_3by2dividor3_1_z1,
       a_3by2dividor3_1_z2, not_1_out, not_2_out;

  not not_1 (not_1_out, X1);
  A_3by2dividor1 a_3by2dividor1_1 (
    .Y2(Y2), .Y1(Y1), .Y0(Y0), .X1(X1), .X0(X0), .Z0(a_3by2dividor1_1_z0), .Z1(a_3by2dividor1_1_z1),
    .Z2(a_3by2dividor1_1_z2));
  A_3by2dividor2 a_3by2dividor2_1 (
    .Y2(Y2), .Y1(Y1), .Y0(Y0), .X1(X1), .X0(X0), .Z0(a_3by2dividor2_1_z0), .Z1(a_3by2dividor2_1_z1),
    .Z2(a_3by2dividor2_1_z2));
  A_3by2dividor3 a_3by2dividor3_1 (
    .Y2(Y2), .Y1(Y1), .Y0(Y0), .X1(X1), .X0(X0), .Z0(a_3by2dividor3_1_z0), .Z1(a_3by2dividor3_1_z1),
    .Z2(a_3by2dividor3_1_z2));
  not not_2 (not_2_out, X0);
  and and_1 (Error, not_1_out, not_2_out);
  or or_1 (Z2, a_3by2dividor3_1_z2, a_3by2dividor2_1_z2, a_3by2dividor1_1_z2);
  or or_2 (Z1, a_3by2dividor1_1_z1, a_3by2dividor2_1_z1, a_3by2dividor3_1_z1);
  or or_3 (Z0, a_3by2dividor1_1_z0, a_3by2dividor2_1_z0, a_3by2dividor3_1_z0);

  // Notes on the sheet:
  //   Dividend (3 bits: Y2 Y1 Y0)
  //   Divisor (2 bits: X1 X0)
  //   Quotient (4 bits: Z2 Z1 Z0 and Error)
  //   3-by-2-bit DIVIDER circuit
endmodule

module A_2bit_decoder (
);


  // Notes on the sheet:
  //   2-bit DECODER circuit (extra credit - see hw)
endmodule

module A_12nGb_memory (
);


  // Notes on the sheet:
  //   12 nanogigabit MEMORY circuit (extra credit - see hw)
endmodule

module A_4x1_multiplier (
  input  in_3,
  input  in_2,
  input  in_1,
  input  in_0,
  input  mult_bit,
  output out_0,
  output out_1,
  output out_2,
  output out_3
);

  and and_1 (out_0, mult_bit, in_0);
  and and_2 (out_1, mult_bit, in_1);
  and and_3 (out_2, mult_bit, in_2);
  and and_4 (out_3, mult_bit, in_3);
endmodule

module A_3by2dividor1 (
  input  Y2,
  input  Y1,
  input  Y0,
  input  X1,
  input  X0,
  output Z0,
  output Z1,
  output Z2
);

  wire not_1_out;

  not not_1 (not_1_out, X1);
  and and_1 (Z0, X0, Y0, not_1_out);
  and and_2 (Z1, X0, Y1, not_1_out);
  and and_3 (Z2, X0, Y2, not_1_out);
endmodule

module A_3by2dividor2 (
  input  Y2,
  input  Y1,
  input  Y0,
  input  X1,
  input  X0,
  output Z0,
  output Z1,
  output Z2
);

  wire not_1_out, not_2_out;

  not not_1 (not_1_out, X1);
  not not_2 (not_2_out, X0);
  and and_1 (Z0, not_2_out, Y1);
  and and_2 (Z1, X1, Y2);

  assign Z2 = 1'b0;
endmodule

module A_3by2dividor3 (
  input  Y2,
  input  Y1,
  input  Y0,
  input  X1,
  input  X0,
  output Z0,
  output Z1,
  output Z2
);

  wire and_1_out, and_2_out, and_3_out, and_4_out, and_5_out, not_1_out, not_2_out, not_3_out, not_4_out,
       not_5_out;

  not not_1 (not_1_out, Y2);
  not not_2 (not_2_out, Y1);
  not not_3 (not_3_out, Y0);
  not not_4 (not_4_out, X1);
  not not_5 (not_5_out, X0);
  and and_1 (and_1_out, X0, X1, Y1, not_1_out, Y0);
  and and_2 (and_2_out, Y2, X0, not_3_out, X1, not_2_out);
  and and_3 (and_3_out, X0, X1, Y2, Y0, not_2_out);
  and and_4 (and_4_out, X0, Y1, not_3_out, Y2, X1);
  and and_5 (and_5_out, X0, Y2, Y1, Y0, X1);
  or or_1 (Z0, and_1_out, and_2_out, and_3_out);
  or or_2 (Z1, and_4_out, and_5_out);

  assign Z2 = 1'b0;
endmodule
